// Logisim project 5_刘佳涌_主文件.circ as structural Verilog: 6 circuits, main circuit pong_final
module ClockDivider (
  input  clk_input,
  input  rst_global,
  output clk_key,
  output clk_ball,
  output clk_score,
  output clk_screen
);


  assign clk_ball = clk_input;
  assign clk_key = clk_input;
  assign clk_score = clk_input;
  assign clk_screen = clk_input;

  // Other names for the same wires on the sheet: CLKI = clk_input; RSTI = rst_global

  // Notes on the sheet:
  //   将1份时间分成4份，美观以及防止冲突
endmodule

module Paddle (
  input  clk_key,
  input  rst_global,
  input  L_UP,
  input  L_DOWN,
  input  R_UP,
  input  R_DOWN,
  output [2:0] Y_L,
  output [2:0] Y_R
);

  wire E7YL, E7YR;
  wire [2:0] DAYL, DAYR, DLYL, DLYR, NXYL, NXYR, NYL, NYR;

  Multiplexer #(.width(3)) multiplexer_1 (.in0(3'b000), .in1(3'b111), .out(DAYL), .sel(L_UP));
  Multiplexer #(.width(3)) multiplexer_2 (.in0(3'b000), .in1(3'b111), .out(DAYR), .sel(R_UP));
  Multiplexer #(.width(3)) multiplexer_3 (.in0(DAYL), .in1(3'b001), .out(DLYL), .sel(L_DOWN));
  Multiplexer #(.width(3)) multiplexer_4 (.in0(DAYR), .in1(3'b001), .out(DLYR), .sel(R_DOWN));
  Adder #(.width(3)) adder_1 (.a(Y_L), .b(DLYL), .out(NXYL), .cin(1'b0));  // open: cout
  Adder #(.width(3)) adder_2 (.a(Y_R), .b(DLYR), .out(NXYR), .cin(1'b0));  // open: cout
  Comparator #(.mode("unsigned"), .width(3)) comparator_1 (.a(NXYL), .b(3'b111), .eq(E7YL));  // open: gt, lt
  Comparator #(.mode("unsigned"), .width(3)) comparator_2 (.a(NXYR), .b(3'b111), .eq(E7YR));  // open: gt, lt
  Multiplexer #(.width(3)) multiplexer_5 (.in0(NXYL), .in1(Y_L), .out(NYL), .sel(E7YL));
  Multiplexer #(.width(3)) multiplexer_6 (.in0(NXYR), .in1(Y_R), .out(NYR), .sel(E7YR));
  Register #(.width(3)) register_1 (.D(NYL), .en(1'b1), .Q(Y_L), .clk(clk_key), .clr(rst_global));
  Register #(.width(3)) register_2 (.D(NYR), .en(1'b1), .Q(Y_R), .clk(clk_key), .clr(rst_global));

  // Other names for the same wires on the sheet: CLK = clk_key; LDN = L_DOWN; LUP = L_UP; RDN = R_DOWN;
  //   RST = rst_global; RUP = R_UP; YL[2:0] = Y_L; YR[2:0] = Y_R

  // Notes on the sheet:
  //   常量：
  //   输入的信号
  //   先判断是否输入，输入传递常量7，未输入传递常量0
  //   挡板按键控制模块
  //   传递来的值可能有0、1、7
  //   0代表没有操作
  //   1代表应该下降
  //   7代表应该上升
  //   利用加法器特性进行坐标计算
  //   当y为0时上升，加法器+3位宽特性会将nxyl最终变为7
  //   当y为6时下降，加法器+3位宽特性会将nxyl最终变为7
  //   这里的7是二相性的，原先可能为0或7，所以需要剔除
  //   这导致到达不了7，但挡板宽度为2
  //   且向下延伸一格，所以这个问题不是问题
  //   不为7，则改变，为7，则不变
  //   常量：
  //   随时间输出实时的y值
  //   yl和yr，即左右高度初始化均为0
endmodule

module Ball (
  input  clk_ball,
  input  rst_global,
  input  game_lock,
  input  [2:0] Y_L,
  input  [2:0] Y_R,
  output [2:0] ball_x,
  output [2:0] ball_y,
  output score_L_pulse,
  output score_R_pulse
);

  wire ATB, ATL, ATR, ATT, EBYL, EBYL1, EBYR, EBYR1, FLIPX, FLIPY, FY0, FY1, HITL, HITR, MISS, NHITL, NHITR,
       NLOCK, NMR, NVX, NVY, OYL, OYR, VX, VXF, VXN, VY, VYN;
  wire [2:0] BXD, BXN, BYD, DX, DY, YL1, YR1;

  not not_1 (NVY, VY);
  not not_2 (NVX, VX);
  not not_3 (NLOCK, game_lock);
  Adder #(.width(3)) adder_1 (.a(Y_L), .b(3'b001), .out(YL1), .cin(1'b0));  // open: cout
  Adder #(.width(3)) adder_2 (.a(Y_R), .b(3'b001), .out(YR1), .cin(1'b0));  // open: cout
  Comparator #(.mode("unsigned"), .width(3)) comparator_1 (.a(ball_y), .b(Y_L), .eq(EBYL));  // open: gt, lt
  Comparator #(.mode("unsigned"), .width(3)) comparator_2 (.a(ball_y), .b(YL1), .eq(EBYL1));  // open: gt, lt
  Comparator #(.mode("unsigned"), .width(3)) comparator_3 (.a(ball_y), .b(Y_R), .eq(EBYR));  // open: gt, lt
  Comparator #(.mode("unsigned"), .width(3)) comparator_4 (.a(ball_y), .b(YR1), .eq(EBYR1));  // open: gt, lt
  Comparator #(.mode("unsigned"), .width(3)) comparator_5 (.a(ball_y), .b(3'b000), .eq(ATT));  // open: gt, lt
  Comparator #(.mode("unsigned"), .width(3)) comparator_6 (.a(ball_y), .b(3'b111), .eq(ATB));  // open: gt, lt
  Comparator #(.mode("unsigned"), .width(3)) comparator_7 (.a(ball_x), .b(3'b000), .eq(ATL));  // open: gt, lt
  or or_1 (OYL, EBYL, EBYL1);
  Comparator #(.mode("unsigned"), .width(3)) comparator_8 (.a(ball_x), .b(3'b111), .eq(ATR));  // open: gt, lt
  or or_2 (OYR, EBYR, EBYR1);
  and and_1 (FY0, ATT, NVY);
  and and_2 (FY1, ATB, VY);
  or or_3 (FLIPY, FY0, FY1);
  and and_3 (HITL, ATL, OYL);
  and and_4 (HITR, ATR, OYR);
  not not_4 (NHITL, HITL);
  not not_5 (NHITR, HITR);
  Multiplexer multiplexer_1 (.in0(VY), .in1(NVY), .out(VYN), .sel(FLIPY));
  Register #(.width(1)) register_1 (.D(VYN), .en(NLOCK), .Q(VY), .clk(clk_ball), .clr(rst_global));
  or or_4 (FLIPX, HITL, HITR);
  and and_5 (score_R_pulse, ATL, NHITL);
  and and_6 (score_L_pulse, ATR, NHITR);
  Multiplexer #(.width(3)) multiplexer_2 (.in0(3'b111), .in1(3'b001), .out(DX), .sel(VXN));
  or or_5 (MISS, score_R_pulse, score_L_pulse);
  Multiplexer #(.width(3)) multiplexer_3 (.in0(3'b111), .in1(3'b001), .out(DY), .sel(VYN));
  Adder #(.width(3)) adder_3 (.a(ball_x), .b(DX), .out(BXD), .cin(1'b0));  // open: cout
  not not_6 (NMR, score_L_pulse);
  Adder #(.width(3)) adder_4 (.a(ball_y), .b(DY), .out(BYD), .cin(1'b0));  // open: cout
  Multiplexer #(.width(3)) multiplexer_4 (.in0(BXD), .in1(3'b011), .out(BXN), .sel(MISS));
  Multiplexer multiplexer_5 (.in0(VXF), .in1(NMR), .out(VXN), .sel(MISS));
  Register #(.width(1)) register_2 (.D(VXN), .en(NLOCK), .Q(VX), .clk(clk_ball), .clr(rst_global));
  Register #(.width(3)) register_3 (.D(BYD), .en(NLOCK), .Q(ball_y), .clk(clk_ball), .clr(rst_global));
  Register #(.width(3)) register_4 (.D(BXN), .en(NLOCK), .Q(ball_x), .clk(clk_ball), .clr(rst_global));
  Multiplexer multiplexer_6 (.in0(VX), .in1(NVX), .out(VXF), .sel(FLIPX));

  // Other names for the same wires on the sheet: BX[2:0] = ball_x; BY[2:0] = ball_y; CLK = clk_ball; LOCK = game_lock;
  //   MISSL = score_R_pulse; MISSR = score_L_pulse; RST = rst_global; YL[2:0] = Y_L; YR[2:0] = Y_R

  // Notes on the sheet:
  //   挡板坐标
  //   小球碰撞模块
  //   NVX、NVY、NLOCK
  //   常量
  //   YL1为左挡板y轴位置+1
  //   即挡板向下延伸了一格
  //   判断球是否与挡板同y轴
  //   这里判断球是否触及上下边界
  //   NVY与VY一个为1另一个为0
  //   判断球是否位于左边界
  //   如果与左挡板y轴相同
  //   判断球是否位于右边界
  //   如果与右挡板y轴相同
  //   与门判断是为了只在球y轴速度"正撞向墙"时翻转，离开墙时绝不翻转
  //   与挡板是否相撞
  //   VYN、VY、FLIPY
  //   相撞时FLIPX为1
  //   VYN用于存储当前速度方向
  //   在有效碰撞上下边界后反向
  //   开始时寄存器会令VY为0
  //   后面会令VY=VYN
  //   球的初始位置不需要额外电路确认——当 rst_global 复位信号有效时，BX/BY 寄存器会被直接置为 Logisim 寄存器属性里设置的"reset value"固定值（通常就是场地中心，比如 BX=4、BY=中间行），一松开复位球就从那里开始移动。
  //   FLIPX
  //   左边不相撞则missl
  //   右边不相撞则missr
  //   同上
  //   根据当前速度方向，DY会在001和111之间变化
  //   BXN、BXD、BX、DX
  //   VXN
  //   DY、BYD、BY
  //   每一时刻存储当前坐标，并与前面的加法器形成正反馈现象
  //   VX、VXF
  //   与挡板相撞时（FLIPX=1），NVX即VX取反，x方向速度相当于反向
  //   将变化后的BXN存进BX
  //   miss时，若右边miss，VXN为0，否则为1；未miss时，VXN始终等于VXF
  //   初始时，寄存器和多路选择器会令VX、VXF为0，由于上面那个VXN始终等于VXF，所以VXN初始也为0
  //   最关键的是VX=0并不代表没有速度，而是与VX=1时的速度等大反向，这是位宽为1只有0与1的速度设计的精髓，小球不会停止
  //   OUTPUT1
  //   OUTPUT2
  //   OUTPUT3
endmodule

module Matrix_Display (
  input  clk_screen,
  input  [2:0] ball_x,
  input  [2:0] ball_y,
  input  [2:0] Y_L,
  input  [2:0] Y_R,
  output [7:0] R0,
  output [7:0] R1,
  output [7:0] R2,
  output [7:0] R3,
  output [7:0] R4,
  output [7:0] R5,
  output [7:0] R6,
  output [7:0] R7
);

  wire BYR0, BYR1, BYR2, BYR3, BYR4, BYR5, BYR6, BYR7, PL0, PL1, PL2, PL3, PL4, PL5, PL6, PL7, PR0, PR1, PR2,
       PR3, PR4, PR5, PR6, PR7, YL1R0, YL1R1, YL1R2, YL1R3, YL1R4, YL1R5, YL1R6, YL1R7, YLR0, YLR1, YLR2,
       YLR3, YLR4, YLR5, YLR6, YLR7, YR1R0, YR1R1, YR1R2, YR1R3, YR1R4, YR1R5, YR1R6, YR1R7, YRR0, YRR1,
       YRR2, YRR3, YRR4, YRR5, YRR6, YRR7;
  wire [2:0] YL1, YR1;
  wire [7:0] BR0, BR1, BR2, BR3, BR4, BR5, BR6, BR7, OH, PLB0, PLB1, PLB2, PLB3, PLB4, PLB5, PLB6, PLB7,
       PRB0, PRB1, PRB2, PRB3, PRB4, PRB5, PRB6, PRB7, TMP0, TMP1, TMP2, TMP3, TMP4, TMP5, TMP6, TMP7;

  or or_1 (PL0, YLR0, YL1R0);
  Multiplexer #(.width(8)) multiplexer_1 (.in0({8{1'b0}}), .in1(OH), .out(BR1), .sel(BYR1));
  or or_2 (PL1, YLR1, YL1R1);
  or or_3 (PL2, YLR2, YL1R2);
  Multiplexer #(.width(8)) multiplexer_2 (.in0({8{1'b0}}), .in1(OH), .out(BR0), .sel(BYR0));
  Multiplexer #(.width(8)) multiplexer_3 (.in0({8{1'b0}}), .in1(8'h80), .out(PLB0), .sel(PL0));
  Multiplexer #(.width(8)) multiplexer_4 (.in0({8{1'b0}}), .in1(8'h80), .out(PLB1), .sel(PL1));
  Multiplexer #(.width(8)) multiplexer_5 (.in0({8{1'b0}}), .in1(OH), .out(BR2), .sel(BYR2));
  Multiplexer #(.width(8)) multiplexer_6 (.in0({8{1'b0}}), .in1(8'h80), .out(PLB2), .sel(PL2));
  Multiplexer #(.width(8)) multiplexer_7 (.in0({8{1'b0}}), .in1(8'h80), .out(PLB3), .sel(PL3));
  or or_4 (PL3, YLR3, YL1R3);
  Decoder #(.enable("false"), .select(3)) decoder_1 (
    .out0(YLR0), .out1(YLR1), .out2(YLR2), .out3(YLR3), .out4(YLR4), .out5(YLR5), .out6(YLR6), .out7(YLR7),
    .sel(Y_L));
  Multiplexer #(.width(8)) multiplexer_8 (.in0({8{1'b0}}), .in1(8'h1), .out(PRB1), .sel(PR1));
  or or_5 (PR1, YRR1, YR1R1);
  or or_6 (PR2, YRR2, YR1R2);
  Multiplexer #(.width(8)) multiplexer_9 (.in0({8{1'b0}}), .in1(OH), .out(BR3), .sel(BYR3));
  assign TMP1 = BR1 | PLB1;  // OR_Gate or_7, 8 bits wide
  assign TMP2 = BR2 | PLB2;  // OR_Gate or_8, 8 bits wide
  Multiplexer #(.width(8)) multiplexer_10 (.in0({8{1'b0}}), .in1(8'h1), .out(PRB2), .sel(PR2));
  or or_9 (PR3, YRR3, YR1R3);
  assign TMP0 = BR0 | PLB0;  // OR_Gate or_10, 8 bits wide
  Multiplexer #(.width(8)) multiplexer_11 (.in0({8{1'b0}}), .in1(8'h1), .out(PRB0), .sel(PR0));
  or or_11 (PR0, YRR0, YR1R0);
  assign TMP3 = BR3 | PLB3;  // OR_Gate or_12, 8 bits wide
  Multiplexer #(.width(8)) multiplexer_12 (.in0({8{1'b0}}), .in1(8'h1), .out(PRB3), .sel(PR3));
  Multiplexer #(.select(3), .width(8)) multiplexer_13 (
    .in0(8'h80), .in1(8'h40), .in2(8'h20), .in3(8'h10), .in4(8'h8), .in5(8'h4), .in6(8'h2), .in7(8'h1),
    .out(OH), .sel(ball_x));
  assign R1 = TMP1 | PRB1;  // OR_Gate or_13, 8 bits wide
  Adder #(.width(3)) adder_1 (.a(Y_L), .b(3'b001), .out(YL1), .cin(1'b0));  // open: cout
  assign R2 = TMP2 | PRB2;  // OR_Gate or_14, 8 bits wide
  assign R0 = TMP0 | PRB0;  // OR_Gate or_15, 8 bits wide
  assign R3 = TMP3 | PRB3;  // OR_Gate or_16, 8 bits wide
  Decoder #(.enable("false"), .select(3)) decoder_2 (
    .out0(YL1R0), .out1(YL1R1), .out2(YL1R2), .out3(YL1R3), .out4(YL1R4), .out5(YL1R5), .out6(YL1R6),
    .out7(YL1R7), .sel(YL1));
  Decoder #(.enable("false"), .select(3)) decoder_3 (
    .out0(BYR0), .out1(BYR1), .out2(BYR2), .out3(BYR3), .out4(BYR4), .out5(BYR5), .out6(BYR6), .out7(BYR7),
    .sel(ball_y));
  or or_17 (PL5, YLR5, YL1R5);
  Multiplexer #(.width(8)) multiplexer_14 (.in0({8{1'b0}}), .in1(8'h80), .out(PLB4), .sel(PL4));
  or or_18 (PL4, YLR4, YL1R4);
  Multiplexer #(.width(8)) multiplexer_15 (.in0({8{1'b0}}), .in1(OH), .out(BR5), .sel(BYR5));
  Multiplexer #(.width(8)) multiplexer_16 (.in0({8{1'b0}}), .in1(8'h80), .out(PLB5), .sel(PL5));
  or or_19 (PL6, YLR6, YL1R6);
  Decoder #(.enable("false"), .select(3)) decoder_4 (
    .out0(YRR0), .out1(YRR1), .out2(YRR2), .out3(YRR3), .out4(YRR4), .out5(YRR5), .out6(YRR6), .out7(YRR7),
    .sel(Y_R));
  Multiplexer #(.width(8)) multiplexer_17 (.in0({8{1'b0}}), .in1(OH), .out(BR4), .sel(BYR4));
  or or_20 (PR5, YRR5, YR1R5);
  Multiplexer #(.width(8)) multiplexer_18 (.in0({8{1'b0}}), .in1(OH), .out(BR6), .sel(BYR6));
  Multiplexer #(.width(8)) multiplexer_19 (.in0({8{1'b0}}), .in1(8'h80), .out(PLB6), .sel(PL6));
  Multiplexer #(.width(8)) multiplexer_20 (.in0({8{1'b0}}), .in1(8'h1), .out(PRB4), .sel(PR4));
  or or_21 (PR4, YRR4, YR1R4);
  assign TMP5 = BR5 | PLB5;  // OR_Gate or_22, 8 bits wide
  Multiplexer #(.width(8)) multiplexer_21 (.in0({8{1'b0}}), .in1(8'h1), .out(PRB5), .sel(PR5));
  or or_23 (PR6, YRR6, YR1R6);
  assign TMP4 = BR4 | PLB4;  // OR_Gate or_24, 8 bits wide
  assign TMP6 = BR6 | PLB6;  // OR_Gate or_25, 8 bits wide
  Multiplexer #(.width(8)) multiplexer_22 (.in0({8{1'b0}}), .in1(8'h1), .out(PRB6), .sel(PR6));
  assign R5 = TMP5 | PRB5;  // OR_Gate or_26, 8 bits wide
  Adder #(.width(3)) adder_2 (.a(Y_R), .b(3'b001), .out(YR1), .cin(1'b0));  // open: cout
  assign R4 = TMP4 | PRB4;  // OR_Gate or_27, 8 bits wide
  assign R6 = TMP6 | PRB6;  // OR_Gate or_28, 8 bits wide
  Decoder #(.enable("false"), .select(3)) decoder_5 (
    .out0(YR1R0), .out1(YR1R1), .out2(YR1R2), .out3(YR1R3), .out4(YR1R4), .out5(YR1R5), .out6(YR1R6),
    .out7(YR1R7), .sel(YR1));
  or or_29 (PL7, YLR7, YL1R7);
  Multiplexer #(.width(8)) multiplexer_23 (.in0({8{1'b0}}), .in1(OH), .out(BR7), .sel(BYR7));
  Multiplexer #(.width(8)) multiplexer_24 (.in0({8{1'b0}}), .in1(8'h80), .out(PLB7), .sel(PL7));
  or or_30 (PR7, YRR7, YR1R7);
  assign TMP7 = BR7 | PLB7;  // OR_Gate or_31, 8 bits wide
  Multiplexer #(.width(8)) multiplexer_25 (.in0({8{1'b0}}), .in1(8'h1), .out(PRB7), .sel(PR7));
  assign R7 = TMP7 | PRB7;  // OR_Gate or_32, 8 bits wide

  // Other names for the same wires on the sheet: BX[2:0] = ball_x; BY[2:0] = ball_y; CS = clk_screen; ROW0[7:0] = R0;
  //   ROW1[7:0] = R1; ROW2[7:0] = R2; ROW3[7:0] = R3; ROW4[7:0] = R4; ROW5[7:0] = R5; ROW6[7:0] = R6; ROW7[7:0] = R7;
  //   YL[2:0] = Y_L; YR[2:0] = Y_R

  // Notes on the sheet:
  //   80：01010000
  //   40：00101000
  //   20：00010100
  //   10：00001010
  //   8：00001000
  //   4：00000100
  //   2：00000010
  //   1：00000001
  //   00000010：2；00000100：4；00001000：8；00010000：16；
  //   00100000：32；01000000：64；10000000：128
  //   但这是16进制（0xXX...）
  //   0x80：10000000
  //   0x40：01000000
  //   0x20：00100000
  //   0x10：00010000
  //   8：00001000
  //   4：00000100
  //   2：00000010
  //   1：00000001
  //   YLRX
  //   左挡板位置
  //   OH
  //   YL1
  //   左挡板位置
  //   8×8点阵行列扫描驱动模块
  //   YL1RX
  //   左挡板位置
  //   BYRX
  //   YRRX
  //   右挡板位置
  //   YR1
  //   右挡板位置
  //   YR1RX
  //   右挡板位置
  //   8bit-0
  //   取决于球当前横坐标
  //   当左挡板在y=7上存在时
  //   当球的y=7时，取当前横坐标
  //   当右挡板在y=7上存在时
  //   融合左挡板与可能存在的坐标
  //   PLB7在PL7=1时为8-bit80（10000000），否则为0
  //   融合挡板与球可能存在的坐标
  //   0x80：10000000
  //   0x40：01000000
  //   0x20：00100000
  //   0x10：00010000
  //   8：00001000
  //   4：00000100
  //   2：00000010
  //   1：00000001
  //   作为显示内容输出
endmodule

module Score_FSM (
  input  clk_score,
  input  rst_global,
  input  score_L_pulse,
  input  score_R_pulse,
  output [3:0] score_L,
  output [3:0] score_R,
  output game_lock
);

  wire GTL, GTR, NLOCK;
  wire [3:0] NSL, NSR, SL1, SR1;

  not not_1 (NLOCK, game_lock);
  Adder #(.width(4)) adder_1 (.a(score_L), .b(4'b0001), .out(SL1), .cin(1'b0));  // open: cout
  Adder #(.width(4)) adder_2 (.a(score_R), .b(4'b0001), .out(SR1), .cin(1'b0));  // open: cout
  Multiplexer #(.width(4)) multiplexer_1 (.in0(score_L), .in1(SL1), .out(NSL), .sel(score_L_pulse));
  Multiplexer #(.width(4)) multiplexer_2 (.in0(score_R), .in1(SR1), .out(NSR), .sel(score_R_pulse));
  Comparator #(.mode("unsigned"), .width(4)) comparator_1 (.a(score_L), .b(4'b0110), .gt(GTL));  // open: eq, lt
  Comparator #(.mode("unsigned"), .width(4)) comparator_2 (.a(score_R), .b(4'b0110), .gt(GTR));  // open: eq, lt
  Register #(.width(4)) register_1 (.D(NSL), .en(NLOCK), .Q(score_L), .clk(clk_score), .clr(rst_global));
  Register #(.width(4)) register_2 (.D(NSR), .en(NLOCK), .Q(score_R), .clk(clk_score), .clr(rst_global));
  or or_1 (game_lock, GTL, GTR);

  // Other names for the same wires on the sheet: CLK = clk_score; LOCK = game_lock; PL = score_L_pulse;
  //   PR = score_R_pulse; RST = rst_global; SL[3:0] = score_L; SR[3:0] = score_R

  // Notes on the sheet:
  //   左侧得分
  //   右侧得分
  //   持续将SL+1的值赋予SL1
  //   同上
  //   判断是否应该为左侧加分
  //   谁先得到7分，谁就获胜
  //   计分游戏状态模块
  //   将保存在NSL的分数计入SL
endmodule

module pong_final (
);

  wire CKBALL, CKKEY, CKSCORE, CKSCR, CLK, keyboard_1_avail, KI, KK, KR, KS, KW, LDN, LDNB, LOCK, LUP, LUPB,
       RDN, RDNB, RST, RSTB, RUP, RUPB, SPL, SPR;
  wire [2:0] BX, BY, YL, YR;
  wire [3:0] SL, SR;
  wire [6:0] ASCII, UPPER;
  wire [7:0] ROW0, ROW1, ROW2, ROW3, ROW4, ROW5, ROW6, ROW7;

  Clock clock_1 (.out(CLK));
  Paddle paddle_1 (
    .clk_key(CKKEY), .rst_global(RST), .L_UP(LUP), .L_DOWN(LDN), .R_UP(RUP), .R_DOWN(RDN), .Y_L(YL), .Y_R(YR));
  Ball ball_1 (
    .clk_ball(CKBALL), .rst_global(RST), .game_lock(LOCK), .Y_L(YL), .Y_R(YR), .ball_x(BX), .ball_y(BY),
    .score_L_pulse(SPL), .score_R_pulse(SPR));
  ClockDivider clockdivider_1 (
    .clk_input(CLK), .rst_global(RST), .clk_key(CKKEY), .clk_ball(CKBALL), .clk_score(CKSCORE),
    .clk_screen(CKSCR));
  Matrix_Display matrix_display_1 (
    .clk_screen(CKSCR), .ball_x(BX), .ball_y(BY), .Y_L(YL), .Y_R(YR), .R0(ROW0), .R1(ROW1), .R2(ROW2),
    .R3(ROW3), .R4(ROW4), .R5(ROW5), .R6(ROW6), .R7(ROW7));
  Score_FSM score_fsm_1 (
    .clk_score(CKSCORE), .rst_global(RST), .score_L_pulse(SPL), .score_R_pulse(SPR), .score_L(SL),
    .score_R(SR), .game_lock(LOCK));
  Hex_Digit_Display hex_digit_display_1 (.value(SL));  // open: dp
  DotMatrix #(.inputtype("row"), .matrixcols(8), .matrixrows(8)) dotmatrix_1 (
    .row0(ROW0), .row1(ROW1), .row2(ROW2), .row3(ROW3), .row4(ROW4), .row5(ROW5), .row6(ROW6), .row7(ROW7));
  LED led_1 (.in(LOCK));
  Keyboard #(.trigger("falling")) keyboard_1 (.clk(CLK), .re(1'b1), .clr(1'b0), .avail(keyboard_1_avail), .data(ASCII));
  Hex_Digit_Display hex_digit_display_2 (.value(SR));  // open: dp
  LED led_2 (.in(keyboard_1_avail));
  Button button_1 (.out(RSTB));
  Button button_2 (.out(LUPB));
  LED led_3 (.in(LUPB));
  Button button_3 (.out(LDNB));
  LED led_4 (.in(LDNB));
  Button button_4 (.out(RUPB));
  LED led_5 (.in(RUPB));
  Button button_5 (.out(RDNB));
  LED led_6 (.in(RDNB));
  assign UPPER = ASCII & 7'b1011111;  // AND_Gate and_1, 7 bits wide
  Comparator #(.mode("unsigned"), .width(7)) comparator_1 (.a(UPPER), .b(7'b1010111), .eq(KW));  // open: gt, lt
  Comparator #(.mode("unsigned"), .width(7)) comparator_2 (.a(UPPER), .b(7'b1010011), .eq(KS));  // open: gt, lt
  Comparator #(.mode("unsigned"), .width(7)) comparator_3 (.a(UPPER), .b(7'b1001001), .eq(KI));  // open: gt, lt
  Comparator #(.mode("unsigned"), .width(7)) comparator_4 (.a(UPPER), .b(7'b1001011), .eq(KK));  // open: gt, lt
  Comparator #(.mode("unsigned"), .width(7)) comparator_5 (.a(UPPER), .b(7'b1010010), .eq(KR));  // open: gt, lt
  or or_1 (LUP, LUPB, KW);
  or or_2 (LDN, LDNB, KS);
  or or_3 (RUP, RUPB, KI);
  or or_4 (RDN, RDNB, KK);
  or or_5 (RST, RSTB, KR);

  // Notes on the sheet:
  //   玩法: 1. 开始仿真ctrl+e  2.ctrl+k启动时钟(球会动)  3.Ctrl+1 切手形  4.键盘打字 W/S/I/K/R 或按住按钮
  //   挡板组件
  //   小球运动组件
  //   PONG v6.2 键盘版 - W/S 左挡板 I/K 右挡板 R 复位 (也可按住按钮)
  //   看不到'v6'字样 = 打开的是旧文件!  交互需: Simulate菜单 Simulation Enabled + Auto-Tick Enabled 都打勾
  //   将1份时间分成4份，以便于不同的速度需求以及防止冲突
  //   如此ck开头的变量都是时序变量
  //   8×8点阵行列扫描驱动模块
  //   分数组件
  //   操作：w左挡板上升
  //   r重置游戏
  //   s左挡板下降
  //   i右挡板上升
  //   k右挡板下降
  //   分数 左
  //   键盘: ①输入法切英文(按Shift) ②手形工具点击键盘框(出现光标) ③直接打字 W/S/I/K/R
  //   双人乒乓球
  //   13局7胜
  //   分数 右
  //   游戏结束
  //   rst
  //   L_UP
  //   L_DOWN
  //   R_UP
  //   R_DOWN
  //   缓冲
  //   键盘
  //   95->2：01011111
  //   87->2：01010111
  //   83->2：01010011
  //   57->2：01001001
  //   59->2：01001011
  //   82->2：01010010
  //   键盘输入转化为指令
endmodule
